// Logisim project DLD final project.circ as structural Verilog: 1 circuit, main circuit main
module main (
  input  F1,
  input  F0,
  output a,
  output b,
  output c,
  output d,
  output e,
  output f,
  output g
);

  wire and_1_out, and_2_out, and_3_out, and_4_out, and_5_out, and_6_out, clock_1_out, D0_q, not_1_out,
       not_2_out, not_3_out, not_5_out, not_6_out, or_1_out, or_2_out, xnor_1_out, xor_1_out;

  xor xor_1 (xor_1_out, g, F1);
  xnor xnor_1 (xnor_1_out, g, F1);
  and and_1 (and_1_out, g, D0_q);
  and and_2 (and_2_out, g, F1);
  or or_1 (or_1_out, and_1_out, and_2_out, and_3_out);
  and and_3 (and_3_out, D0_q, F1);
  and and_4 (and_4_out, ~D0_q, F0);  // AND_Gate
  and and_5 (and_5_out, F0, xnor_1_out);
  and and_6 (and_6_out, ~D0_q, xor_1_out);  // AND_Gate
  or or_2 (or_2_out, and_4_out, and_5_out, and_6_out);
  Clock clock_1 (.out(clock_1_out));
  D_Flip_Flop D1 (.clk(clock_1_out), .D(or_1_out), .Q(g));  // open: Qn, preset, en, reset
  D_Flip_Flop D0 (.clk(clock_1_out), .D(or_2_out), .Q(D0_q));  // open: Qn, preset, en, reset
  not not_1 (not_1_out, D0_q);
  not not_2 (not_2_out, g);
  not not_3 (not_3_out, D0_q);
  not not_4 (e, D0_q);
  not not_5 (not_5_out, g);
  not not_6 (not_6_out, D0_q);
  or or_3 (a, not_1_out, g);
  or or_4 (c, not_2_out, D0_q);
  or or_5 (d, not_3_out, g);
  and and_7 (f, not_5_out, not_6_out);
  _7_Segment_Display u_7_segment_display_1 (.g(g), .f(f), .a(a), .b(1'b1), .e(e), .d(d), .c(c));  // open: dp

  assign b = 1'b1;
endmodule
